// Logisim project regfile.circ as structural Verilog: 1 circuit, main circuit regfile
module regfile (
  input  [4:0] ReadReg1,
  input  [4:0] ReadReg2,
  input  [4:0] WriteReg,
  input  [31:0] RegWriteData,
  input  RegWEn,
  input  clk,
  output [31:0] ra,
  output [31:0] sp,
  output [31:0] t0,
  output [31:0] t1,
  output [31:0] t2,
  output [31:0] s0,
  output [31:0] s1,
  output [31:0] a0,
  output [31:0] RegReadData1,
  output [31:0] RegReadData2
);

  wire x0_WEn, x1_WEn, x2_WEn, x3_WEn, x4_WEn, x5_WEn, x6_WEn, x7_WEn, x8_WEn, x9_WEn, x10_WEn, x11_WEn,
       x12_WEn, x13_WEn, x14_WEn, x15_WEn, x16_WEn, x17_WEn, x18_WEn, x19_WEn, x20_WEn, x21_WEn, x22_WEn,
       x23_WEn, x24_WEn, x25_WEn, x26_WEn, x27_WEn, x28_WEn, x29_WEn, x30_WEn, x31_WEn;
  wire [31:0] and_1_out, Dx0, Qx0, Qx3, Qx4, Qx11, Qx12, Qx13, Qx14, Qx15, Qx16, Qx17, Qx18, Qx19, Qx20,
       Qx21, Qx22, Qx23, Qx24, Qx25, Qx26, Qx27, Qx28, Qx29, Qx30, Qx31, x0_q;

  Register #(.width(32)) x16 (.D(RegWriteData), .en(x16_WEn), .clk(clk), .Q(Qx16));  // open: clr
  Register #(.width(32)) x17 (.D(RegWriteData), .en(x17_WEn), .clk(clk), .Q(Qx17));  // open: clr
  Register #(.width(32)) x18 (.D(RegWriteData), .en(x18_WEn), .clk(clk), .Q(Qx18));  // open: clr
  Register #(.width(32)) x19 (.D(RegWriteData), .en(x19_WEn), .clk(clk), .Q(Qx19));  // open: clr
  Register #(.width(32)) x20 (.D(RegWriteData), .en(x20_WEn), .clk(clk), .Q(Qx20));  // open: clr
  Register #(.width(32)) x21 (.D(RegWriteData), .en(x21_WEn), .clk(clk), .Q(Qx21));  // open: clr
  Register #(.width(32)) x22 (.D(RegWriteData), .en(x22_WEn), .clk(clk), .Q(Qx22));  // open: clr
  Register #(.width(32)) x23 (.D(RegWriteData), .en(x23_WEn), .clk(clk), .Q(Qx23));  // open: clr
  Register #(.width(32)) x24 (.D(RegWriteData), .en(x24_WEn), .clk(clk), .Q(Qx24));  // open: clr
  Register #(.width(32)) x25 (.D(RegWriteData), .en(x25_WEn), .clk(clk), .Q(Qx25));  // open: clr
  Register #(.width(32)) x26 (.D(RegWriteData), .en(x26_WEn), .clk(clk), .Q(Qx26));  // open: clr
  Register #(.width(32)) x27 (.D(RegWriteData), .en(x27_WEn), .clk(clk), .Q(Qx27));  // open: clr
  Register #(.width(32)) x28 (.D(RegWriteData), .en(x28_WEn), .clk(clk), .Q(Qx28));  // open: clr
  Register #(.width(32)) x29 (.D(RegWriteData), .en(x29_WEn), .clk(clk), .Q(Qx29));  // open: clr
  Register #(.width(32)) x30 (.D(RegWriteData), .en(x30_WEn), .clk(clk), .Q(Qx30));  // open: clr
  Register #(.width(32)) x31 (.D(RegWriteData), .en(x31_WEn), .clk(clk), .Q(Qx31));  // open: clr
  assign and_1_out = {32{1'b0}} & Dx0;  // AND_Gate and_1, 32 bits wide
  Register #(.width(32)) x0 (.D(and_1_out), .en(x0_WEn), .clk(clk), .Q(x0_q));  // open: clr
  Register #(.width(32)) x1 (.D(RegWriteData), .en(x1_WEn), .clk(clk), .Q(ra));  // open: clr
  Register #(.width(32)) x2 (.D(RegWriteData), .en(x2_WEn), .clk(clk), .Q(sp));  // open: clr
  Register #(.width(32)) x3 (.D(RegWriteData), .en(x3_WEn), .clk(clk), .Q(Qx3));  // open: clr
  Register #(.width(32)) x4 (.D(RegWriteData), .en(x4_WEn), .clk(clk), .Q(Qx4));  // open: clr
  Register #(.width(32)) x5 (.D(RegWriteData), .en(x5_WEn), .clk(clk), .Q(t0));  // open: clr
  Register #(.width(32)) x6 (.D(RegWriteData), .en(x6_WEn), .clk(clk), .Q(t1));  // open: clr
  Register #(.width(32)) x7 (.D(RegWriteData), .en(x7_WEn), .clk(clk), .Q(t2));  // open: clr
  Register #(.width(32)) x8 (.D(RegWriteData), .en(x8_WEn), .clk(clk), .Q(s0));  // open: clr
  Register #(.width(32)) x9 (.D(RegWriteData), .en(x9_WEn), .clk(clk), .Q(s1));  // open: clr
  Register #(.width(32)) x10 (.D(RegWriteData), .en(x10_WEn), .clk(clk), .Q(a0));  // open: clr
  Register #(.width(32)) x11 (.D(RegWriteData), .en(x11_WEn), .clk(clk), .Q(Qx11));  // open: clr
  Register #(.width(32)) x12 (.D(RegWriteData), .en(x12_WEn), .clk(clk), .Q(Qx12));  // open: clr
  Register #(.width(32)) x13 (.D(RegWriteData), .en(x13_WEn), .clk(clk), .Q(Qx13));  // open: clr
  Register #(.width(32)) x14 (.D(RegWriteData), .en(x14_WEn), .clk(clk), .Q(Qx14));  // open: clr
  Register #(.width(32)) x15 (.D(RegWriteData), .en(x15_WEn), .clk(clk), .Q(Qx15));  // open: clr
  assign Qx0 = x0_q & {32{1'b0}};  // AND_Gate and_2, 32 bits wide
  Multiplexer #(.enable("false"), .select(5), .width(32)) multiplexer_1 (
    .in0(Qx0), .in1(ra), .in2(sp), .in3(Qx3), .in4(Qx4), .in5(t0), .in6(t1), .in7(t2), .in8(s0), .in9(s1),
    .in10(a0), .in11(Qx11), .in12(Qx12), .in13(Qx13), .in14(Qx14), .in15(Qx15), .in16(Qx16), .in17(Qx17),
    .in18(Qx18), .in19(Qx19), .in20(Qx20), .in21(Qx21), .in22(Qx22), .in23(Qx23), .in24(Qx24), .in25(Qx25),
    .in26(Qx26), .in27(Qx27), .in28(Qx28), .in29(Qx29), .in30(Qx30), .in31(Qx31), .out(RegReadData1),
    .sel(ReadReg1));
  Multiplexer #(.enable("false"), .select(5), .width(32)) multiplexer_2 (
    .in0(Qx0), .in1(ra), .in2(sp), .in3(Qx3), .in4(Qx4), .in5(t0), .in6(t1), .in7(t2), .in8(s0), .in9(s1),
    .in10(a0), .in11(Qx11), .in12(Qx12), .in13(Qx13), .in14(Qx14), .in15(Qx15), .in16(Qx16), .in17(Qx17),
    .in18(Qx18), .in19(Qx19), .in20(Qx20), .in21(Qx21), .in22(Qx22), .in23(Qx23), .in24(Qx24), .in25(Qx25),
    .in26(Qx26), .in27(Qx27), .in28(Qx28), .in29(Qx29), .in30(Qx30), .in31(Qx31), .out(RegReadData2),
    .sel(ReadReg2));
  Demultiplexer #(.enable("false"), .select(5)) demultiplexer_1 (
    .out0(x0_WEn), .out1(x1_WEn), .out2(x2_WEn), .out3(x3_WEn), .out4(x4_WEn), .out5(x5_WEn), .out6(x6_WEn),
    .out7(x7_WEn), .out8(x8_WEn), .out9(x9_WEn), .out10(x10_WEn), .out11(x11_WEn), .out12(x12_WEn),
    .out13(x13_WEn), .out14(x14_WEn), .out15(x15_WEn), .out16(x16_WEn), .out17(x17_WEn), .out18(x18_WEn),
    .out19(x19_WEn), .out20(x20_WEn), .out21(x21_WEn), .out22(x22_WEn), .out23(x23_WEn), .out24(x24_WEn),
    .out25(x25_WEn), .out26(x26_WEn), .out27(x27_WEn), .out28(x28_WEn), .out29(x29_WEn), .out30(x30_WEn),
    .out31(x31_WEn), .in(RegWEn), .sel(WriteReg));

  // Other names for the same wires on the sheet: Qx1[31:0] = ra; Qx2[31:0] = sp; Qx5[31:0] = t0; Qx6[31:0] = t1;
  //   Qx7[31:0] = t2; Qx8[31:0] = s0; Qx9[31:0] = s1; Qx10[31:0] = a0

  // Notes on the sheet:
  //   INPUTS to your circuit
  //   DON'T CHANGE THE LOCATIONS OF THE INPUTS AND OUTPUTS!
  //   These are DEBUG/TEST outputs from your circuit.
  //   OUTPUTS from your circuit
endmodule
